# Fritzing sketch lm386 amplifier (saved by Fritzing 0.9.3b)
breadboards: 1

parts:
  U1 = MIC [package=mic-9.7mm]
  U2 = LM386 [package=dip08]
  R1 = Resistor [tolerance=±5% resistance=10k package=THT]
  C1 = Electrolytic Capacitor [capacitance=10µF package="100 mil [THT, electrolytic]"]
  C2 = Electrolytic Capacitor [capacitance=10µF package="100 mil [THT, electrolytic]"]
  C3 = Electrolytic Capacitor [capacitance=10µF package="100 mil [THT, electrolytic]"]
  C4 = Electrolytic Capacitor [capacitance=1µF package="100 mil [THT, electrolytic]"]  # not connected
  C5 = Ceramic Capacitor [capacitance=47nF package="100 mil [THT, multilayer]"]
  R2 = Resistor [tolerance=±5% resistance=10 package=THT]

nets:
  N1: U1.1, U2.-IN, U2.V-, C2.-, R2.Pin_1
  N2: U1.2, R1.Pin_0
  N3: U2.GAIN, C3.-, C3.+
  N4: U2.+IN, C1.-
  N5: U2.OUT, C5.0
  N6: U2.V+, R1.Pin_1, C1.+
  N7: U2.BP, C2.+
  N8: C5.1, R2.Pin_0
