# Fritzing sketch sound level (saved by Fritzing 0.9.3b)
circuit board: 8.46667cm x 5.64444cm
breadboards: 1

parts:
  Q1_2N3904 = NPN-Transistor [package="TO92 [THT]"]
  R1 = Resistor [tolerance=±5% resistance=1k package=THT]
  R2 = Resistor [tolerance=±5% resistance=100 package=THT]
  C1 = Ceramic Capacitor [capacitance=22µF package="100 mil [THT, multilayer]"]
  R3 = Resistor [tolerance=±5% resistance=10k package=THT]
  R4 = Resistor [tolerance=±5% resistance=47k package=THT]
  C2 = Ceramic Capacitor [capacitance=2.2µF package="100 mil [THT, multilayer]"]
  U1_Mic = MIC [package=mic_electret_smd]
  R5 = Resistor [tolerance=±5% resistance=10k package=THT]
  Part1 = Arduino Uno (Rev3)
  D1 = Rectifier Diode [part_number=1N4001 package="300 mil [THT]"]
  R6 = Resistor [tolerance=±5% resistance=220 package=THT]
  C3 = Electrolytic Capacitor [capacitance=1µF package="100 mil [THT, electrolytic]"]

nets (from the breadboard view):
  N1: Q1_2N3904.E, R2.Pin_0, C1.0
  N2: Q1_2N3904.B, R2.Pin_1, C1.1, R3.Pin_1, R4.Pin_0, R4.Pin_1, C2.1, U1_Mic.2, Part1.GND
  N3: Q1_2N3904.C, R1.Pin_1, D1.anode
  N4: R1.Pin_0, R3.Pin_0, R5.Pin_0, Part1.5V
  N5: C2.0, R5.Pin_1
  N6: Part1.A0, R6.Pin_1, C3.-
  N7: D1.cathode, R6.Pin_0, C3.+
